# Fritzing sketch basic_button_soc (saved by Fritzing 1.0.1rc)
breadboards: 1

parts:
  R1 = Resistor [tolerance=±5% power=0.25W resistance=330 package=THT]
  S1 = Pushbutton [package="[THT]"]
  A1 = photon2

nets:
  N1: R1.Pin_0, S1.Pin_1, S1.Pin_2, A1.Pin_25
  N2: R1.Pin_1, A1.Pin_4, A1.Pin_30, A1.Pin_32
  N3: S1.Pin_3, S1.Pin_4, A1.Pin_2, A1.Pin_31
  N4: A1.Pin_28, A1.Pin_29

custom parts:
  photon2: The Photon 2 is a development module with a microcontroller and Wi-Fi networking.
