# Fritzing sketch button_led_pulse (saved by Fritzing 1.0.1rc)
breadboards: 1

parts:
  R1 = Resistor [tolerance=±5% power=0.25W resistance=1k package=THT]
  S5 = Pushbutton [package="[SMD]"]
  LED1 = LED - 5mm [color="Green (565nm)" current=0.030A package="5 mm [THT]"]
  A1 = photon2
  R2 = Resistor [tolerance=±5% power=0.25W resistance=10k package=THT]

nets:
  N1: R1.Pin_0, A1.Pin_4, A1.Pin_30, A1.Pin_35, R2.Pin_0
  N2: R1.Pin_1, LED1.cathode
  N3: S5.Pin_1, S5.Pin_2, A1.Pin_23, A1.Pin_37, R2.Pin_1
  N4: S5.Pin_3, S5.Pin_4, A1.Pin_2
  N5: LED1.anode, A1.Pin_24, A1.Pin_36
  N6: A1.Pin_28, A1.Pin_29

custom parts:
  photon2: The Photon 2 is a development module with a microcontroller and Wi-Fi networking.
