# Fritzing sketch potentiometer_oled (saved by Fritzing 1.0.1rc)
breadboards: 1

parts:
  U1 = POT [knob_status=50% power=0.5W package=alps_pot]  # not connected
  U2 = POT [knob_status=50% power=0.5W package=trim_pot]  # not connected
  A1 = photon2
  Part1 = Adafruit OLED Monochrome 1.3in 128x64 with STEMMA QT [part_number="Adafruit #938"]  # not connected

nets:
  N1: A1.Pin_4, A1.Pin_30
  N2: A1.Pin_28, A1.Pin_29

custom parts:
  photon2: The Photon 2 is a development module with a microcontroller and Wi-Fi networking.
  Adafruit OLED Monochrome 1.3in 128x64 with STEMMA QT: These displays are small, only about 1.3" diagonal, but very readable due to the high contrast of an OLED display. This display is made of 128x64 individual white OLED pixels, each one is turned on or off by the controller chip. Because the display makes its own light, no backlight is required. This reduces the power required to run the OLED and is why the display has such high contrast; we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
