# Fritzing sketch publisher (saved by Fritzing 1.0.1rc)
breadboards: 1

parts:
  U1 = POT [knob_status=50% power=0.5W package=alps_pot]
  A1 = photon2
  U2 = LIPO-2000mAh [package=lipo-2000]

nets:
  N1: U1.E, A1.Pin_2, A1.Pin_31
  N2: U1.S, A1.Pin_5
  N3: U1.A, A1.Pin_4, A1.Pin_30, A1.Pin_32, U2.-
  N4: A1.Pin_28, A1.Pin_29, U2.+

custom parts:
  photon2: The Photon 2 is a development module with a microcontroller and Wi-Fi networking.
